// Logisim project assignmnet02DES.circ as structural Verilog: 1 circuit, main circuit main
module main (
);

  wire and_1_out, and_2_out, and_3_out, and_4_out, button_1_out, clock_1_out, nor_1_out, nor_2_out,
       nor_3_out, not_1_out, not_2_out, or_1_out, or_2_out;
  wire [3:0] counter_1_q;
  wire [6:0] rom_1_data;

  Button button_1 (.out(button_1_out));
  or or_1 (or_1_out, button_1_out, not_2_out);
  Counter #(.width(4), .max('h9)) counter_1 (
    .clr(1'b0), .load(button_1_out), .up(1'b0), .count(1'b1), .clk(and_1_out), .D(4'b1001), .Q(counter_1_q));  // open: carry
  Clock clock_1 (.out(clock_1_out));
  and and_1 (and_1_out, clock_1_out, or_1_out);
  and and_2 (and_2_out, counter_1_q[1], counter_1_q[0]);
  not not_1 (not_1_out, counter_1_q[3]);
  nor nor_1 (nor_1_out, counter_1_q[0], counter_1_q[1]);
  nor nor_2 (nor_2_out, counter_1_q[2], counter_1_q[3]);
  ROM #(.addrWidth(4), .dataWidth(7)) rom_1 (.addr(counter_1_q), .data(rom_1_data));
  and and_3 (and_3_out, nor_1_out, nor_2_out);
  not not_2 (not_2_out, and_3_out);
  or or_2 (or_2_out, counter_1_q[2], and_2_out);
  and and_4 (and_4_out, or_2_out, not_1_out);
  nor nor_3 (nor_3_out, and_3_out, and_4_out);
  _7_Segment_Display u_7_segment_display_1 (
    .g(rom_1_data[6]), .f(rom_1_data[5]), .a(rom_1_data[0]), .b(rom_1_data[1]), .e(rom_1_data[4]),
    .d(rom_1_data[3]), .c(rom_1_data[2]));  // open: dp
  LED green (.in(and_3_out));
  LED Orange (.in(nor_3_out));
  LED red (.in(and_4_out));

  // Notes on the sheet:
  //   contents of rom_1 (hex, n*v repeats v):
  //   3f 6 5b 4f 66 6d 7d 7 7f 6f
endmodule
